# Fritzing sketch diagram (saved by Fritzing 1.0.3b)
breadboards: 1

parts:
  U1 = 7-SEGMENT-DISPLAY [package=7-segment-display]
  Mod1 = Raspberry Pi 4B
  R1 = Resistor [tolerance=±5% power=0.25W resistance=220 package=THT]
  R2 = Resistor [tolerance=±5% power=0.25W resistance=220 package=THT]
  R3 = Resistor [tolerance=±5% power=0.25W resistance=220 package=THT]
  R4 = Resistor [tolerance=±5% power=0.25W resistance=220 package=THT]
  R5 = Resistor [tolerance=±5% power=0.25W resistance=220 package=THT]
  R6 = Resistor [tolerance=±5% power=0.25W resistance=220 package=THT]
  R7 = Resistor [tolerance=±5% power=0.25W resistance=220 package=THT]
  R8 = Resistor [tolerance=±5% power=0.25W resistance=220 package=THT]
  IC1 = L293D [package=THT]
  PSU1 = Adjustable Breadboard Power Supply
  M1 = DC Motor [voltage_(max)=6V voltage_(min)=3V]
  J1 = Basic Servo
  S1 = Pushbutton [package="[SMD]"]
  S2 = Pushbutton [package="[SMD]"]
  VCC1 = Battery block 9V [internal_resistance=0.1Ω]
  Adafruit_ADS7830_8-Channel_8-Bit_ADC1 = Adafruit ADS7830 8-Channel 8-Bit ADC [part_number=#5836]
  Part1 = Thumb Joystick

nets:
  N1: U1.E, R8.Pin_1
  N2: U1.D, R2.Pin_1
  N3: U1.G1, R1.Pin_1
  VCC: U1.C, U1.F, Mod1.3V3, IC1.0V, Adafruit_ADS7830_8-Channel_8-Bit_ADC1.VCC, Part1.VCC
  N4: U1.DP, R3.Pin_0
  N5: U1.B, R4.Pin_0
  N6: U1.A, R6.Pin_0
  N7: U1.G2, R5.Pin_0
  N8: U1.G, R7.Pin_1
  N9: Mod1.GPIO2, Adafruit_ADS7830_8-Channel_8-Bit_ADC1.SDA
  N10: Mod1.GPIO3, Adafruit_ADS7830_8-Channel_8-Bit_ADC1.SCL
  GND: Mod1.GND, PSU1.Vin-, J1.gnd, S1.Pin_1, S1.Pin_2, S2.Pin_1, S2.Pin_2, Adafruit_ADS7830_8-Channel_8-Bit_ADC1.GND, Part1.GND
  N11: Mod1.GPIO18, J1.pulse
  N12: Mod1.GPIO27, IC1.In_2
  N13: Mod1.GPIO22, IC1.In_1
  N14: Mod1.GPIO25, S1.Pin_3, S1.Pin_4
  N15: Mod1.GPIO5, S2.Pin_3, S2.Pin_4
  N16: Mod1.GPIO6, R6.Pin_1
  N17: Mod1.GPIO12, R7.Pin_0
  N18: Mod1.GPIO13, R4.Pin_1
  N19: Mod1.GPIO19, R3.Pin_1
  N20: Mod1.GPIO16, R5.Pin_1
  N21: Mod1.GPIO26, R8.Pin_0
  N22: Mod1.GPIO20, R2.Pin_0
  N23: Mod1.GPIO21, R1.Pin_0
  N24: IC1.Enable_1, IC1.+Vmotor, PSU1.Vout+, J1.vcc
  N25: IC1.Out_1_(_Controlled_by_Enable_1_), M1.pin_2
  N26: IC1.Out_2_(_Controlled_by_Enable_1_), M1.pin_1
  N27: PSU1.Vin2+, VCC1.+
  N28: PSU1.Vin2-, VCC1.-
  N29: Adafruit_ADS7830_8-Channel_8-Bit_ADC1.A0, Part1.VERT
  N30: Adafruit_ADS7830_8-Channel_8-Bit_ADC1.A1, Part1.HORZ

custom parts:
  Adafruit ADS7830 8-Channel 8-Bit ADC: Many microcontrollers have ADCs these days, for reading analog/resistive sensors like potentiometers, thermistors, LDR light sensors, etc. but sometimes you need MOAR! Or maybe you're using a single board computer like a Raspberry Pi that has no ADCs at all! The Adafruit ADS7830 8-Channel 8-Bit ADC with I2C is an affordable 8-channel ADC with I2C interface, so it's easy to include with any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
